// Digital circuit ALU.dig as structural Verilog
module ALU (
  input  [15:0] A_in,
  input  [15:0] B_in,
  input  C_in,
  input  [3:0] ContSel,
  input  CLK,
  input  ADD_SUB,
  output [15:0] ALU_out,
  output Zero_output,
  output C_out,
  output Is_equal
);

  wire add_1_c_o, or_2_out, or_3_out, or_4_out, register_1_q, sub_1_c_o;
  wire [0:0] comparator_1_lt;
  wire [15:0] add_1_s, add_2_s, and_1_out, and_2_out, barrelshifter_1_out, barrelshifter_2_out, not_1_out,
       Operand_A_q, Operand_B_q, or_1_out, sub_1_s, sub_2_s;

  Register #(.Bits(16)) Operand_A (.D(A_in), .C(CLK), .en(1'b1), .Q(Operand_A_q));
  Register #(.Bits(16)) Operand_B (.D(B_in), .C(CLK), .en(1'b1), .Q(Operand_B_q));
  Register register_1 (.D(C_in), .C(CLK), .en(1'b1), .Q(register_1_q));
  Add #(.Bits(16)) add_1 (.a(Operand_A_q), .b(Operand_B_q), .c_i(register_1_q), .s(add_1_s), .c_o(add_1_c_o));
  Sub #(.Bits(16)) sub_1 (.a(Operand_A_q), .b(Operand_B_q), .c_i(register_1_q), .s(sub_1_s), .c_o(sub_1_c_o));
  Comparator #(.Bits(16)) comparator_1 (
    .a(Operand_A_q), .b(Operand_B_q), .eq(Is_equal), .lt(comparator_1_lt[0]));  // open: gt
  assign and_1_out = Operand_A_q & Operand_B_q;  // And and_1, 16 bits wide
  assign or_1_out = Operand_A_q | Operand_B_q;  // Or or_1, 16 bits wide
  assign not_1_out = ~Operand_A_q;  // Not not_1, 16 bits wide
  BarrelShifter #(.Bits(16), .barrelShifterMode("rotate")) barrelshifter_1 (
    .in(Operand_A_q), .shift(Operand_B_q[4:0]), .out(barrelshifter_1_out));
  BarrelShifter #(.Bits(16), .direction("right")) barrelshifter_2 (
    .in(Operand_A_q), .shift(Operand_B_q[4:0]), .out(barrelshifter_2_out));
  Add #(.Bits(16)) add_2 (.a(Operand_A_q), .b(16'h1), .c_i(1'b0), .s(add_2_s));  // open: c_o
  Sub #(.Bits(16)) sub_2 (.a(Operand_A_q), .b(16'h1), .c_i(1'b0), .s(sub_2_s));  // open: c_o
  assign and_2_out = Operand_A_q & {16{1'b0}};  // And and_2, 16 bits wide
  Multiplexer #(.Selector_Bits(4), .Bits(16)) multiplexer_1 (
    .sel(ContSel), .in_0(add_1_s), .in_1(sub_1_s), .in_2(Operand_A_q), .in_3(and_1_out), .in_4(or_1_out),
    .in_5(not_1_out), .in_6(barrelshifter_1_out), .in_7(barrelshifter_2_out), .in_8(add_2_s), .in_9(sub_2_s),
    .in_10(and_2_out), .in_11({{15{1'b0}}, comparator_1_lt[0]}), .in_12(Operand_A_q), .in_13(Operand_A_q),
    .in_14({16{1'b0}}), .in_15({16{1'b0}}), .out(ALU_out));
  Multiplexer multiplexer_2 (.sel(ADD_SUB), .in_0(add_1_c_o), .in_1(sub_1_c_o), .out(C_out));
  or or_2 (or_2_out, ALU_out[0], ALU_out[1], ALU_out[2], ALU_out[3], ALU_out[4]);
  or or_3 (or_3_out, ALU_out[5], ALU_out[6], ALU_out[7], ALU_out[8], ALU_out[9]);
  or or_4 (or_4_out, ALU_out[10], ALU_out[11], ALU_out[12], ALU_out[13], ALU_out[14]);
  nor nor_1 (Zero_output, or_2_out, or_3_out, or_4_out, ALU_out[15]);
endmodule
