// Digital circuit Decoder.dig as structural Verilog
module Decoder (
  input  [15:0] Instruction_in,
  input  CLK,
  input  Instruction_enable,
  output Load,
  output Store,
  output Jump,
  output JZ,
  output JC,
  output Halt,
  output JE,
  output JD,
  output ADD,
  output SUB,
  output IsEqual,
  output And,
  output Or,
  output Comp,
  output SL,
  output SR,
  output Inc,
  output Dec,
  output Clr,
  output ClrFlags,
  output SLT,
  output [2:0] RD,
  output [2:0] RS1,
  output [2:0] RS2,
  output [11:0] Address_out,
  output ADD_ALU,
  output ADD_SUB,
  output INR,
  output OUTR
);

  wire and_1_out, and_2_out, and_3_out, and_9_out, decoder_1_out_0, decoder_1_out_1, decoder_2_out_0,
       decoder_2_out_1, decoder_2_out_3, decoder_3_out_0, decoder_3_out_1, decoder_3_out_2, decoder_3_out_3,
       decoder_3_out_4, decoder_3_out_5, decoder_4_out_0, decoder_4_out_1, decoder_4_out_2, decoder_4_out_3,
       decoder_4_out_4, decoder_4_out_5, decoder_4_out_6, or_1_out;
  wire [2:0] Instruction_Register_q;
  wire [15:15] Instruction_Register_q_2;

  Multiplexer #(.Bits(3)) multiplexer_1 (.sel(decoder_1_out_0), .in_0(Address_out[2:0]), .in_1(3'b000), .out(RD));
  Register #(.Bits(16)) Instruction_Register (
    .D(Instruction_in), .C(CLK), .en(Instruction_enable),
    .Q({Instruction_Register_q_2[15], Instruction_Register_q, Address_out}));
  Decoder decoder_1 (.sel(Instruction_Register_q_2[15]), .out_0(decoder_1_out_0), .out_1(decoder_1_out_1));
  Decoder #(.Selector_Bits(2)) decoder_2 (
    .sel(Instruction_Register_q[2:1]), .out_0(decoder_2_out_0), .out_1(decoder_2_out_1),
    .out_3(decoder_2_out_3));  // open: out_2
  Decoder #(.Selector_Bits(3)) decoder_3 (
    .sel({Instruction_Register_q[0], Address_out[11:10]}), .out_0(decoder_3_out_0), .out_1(decoder_3_out_1),
    .out_2(decoder_3_out_2), .out_3(decoder_3_out_3), .out_4(decoder_3_out_4), .out_5(decoder_3_out_5));  // open: out_6, out_7
  Decoder #(.Selector_Bits(3)) decoder_4 (
    .sel(Instruction_Register_q), .out_0(decoder_4_out_0), .out_1(decoder_4_out_1), .out_2(decoder_4_out_2),
    .out_3(decoder_4_out_3), .out_4(decoder_4_out_4), .out_5(decoder_4_out_5), .out_6(decoder_4_out_6));  // open: out_7
  or or_1 (or_1_out, decoder_4_out_1, decoder_4_out_6);
  and and_1 (and_1_out, Address_out[0], Address_out[1], Address_out[2], Address_out[3], Address_out[4]);
  and and_2 (and_2_out, Address_out[5], Address_out[6], Address_out[7], Address_out[8], Address_out[9]);
  and and_3 (and_3_out, Address_out[10], Address_out[11], Instruction_Register_q[0], Instruction_Register_q[1], Instruction_Register_q[2]);
  and and_4 (Load, decoder_1_out_0, decoder_4_out_0);
  and and_5 (Store, decoder_1_out_0, or_1_out);
  and and_6 (Jump, decoder_1_out_0, decoder_4_out_2);
  and and_7 (JZ, decoder_1_out_0, decoder_4_out_3);
  and and_8 (JC, decoder_1_out_0, decoder_4_out_4);
  and and_9 (and_9_out, and_1_out, and_2_out, and_3_out, Instruction_Register_q_2[15]);
  not not_1 (ADD_ALU, decoder_1_out_0);
  and and_10 (JE, decoder_4_out_5, decoder_1_out_0);
  and and_11 (JD, decoder_4_out_6, decoder_1_out_0);
  not not_2 (Halt, and_9_out);
  and and_12 (INR, decoder_1_out_1, decoder_3_out_4, decoder_2_out_3);
  and and_13 (OUTR, decoder_1_out_1, decoder_3_out_5, decoder_2_out_3);
  and and_14 (ADD, decoder_1_out_1, decoder_2_out_0, decoder_3_out_0);
  and and_15 (SUB, decoder_1_out_1, decoder_2_out_0, decoder_3_out_1);
  and and_16 (IsEqual, decoder_1_out_1, decoder_2_out_0, decoder_3_out_2);
  and and_17 (And, decoder_1_out_1, decoder_2_out_0, decoder_3_out_3);
  and and_18 (Or, decoder_1_out_1, decoder_2_out_0, decoder_3_out_4);
  and and_19 (Comp, decoder_1_out_1, decoder_2_out_1, decoder_3_out_0);
  and and_20 (SL, decoder_1_out_1, decoder_2_out_1, decoder_3_out_1);
  and and_21 (SR, decoder_1_out_1, decoder_2_out_1, decoder_3_out_2);
  and and_22 (Inc, decoder_1_out_1, decoder_2_out_3, decoder_3_out_0);
  and and_23 (Dec, decoder_1_out_1, decoder_2_out_3, decoder_3_out_1);
  and and_24 (Clr, decoder_1_out_1, decoder_2_out_3, decoder_3_out_2);
  and and_25 (ClrFlags, decoder_1_out_1, decoder_2_out_3, decoder_3_out_3);
  and and_26 (SLT, decoder_1_out_1, decoder_2_out_0, decoder_3_out_5);
  PriorityEncoder priorityencoder_1 (.in0(ADD), .in1(SUB), .num(ADD_SUB));  // open: any

  assign RS1 = Address_out[5:3];
  assign RS2 = Address_out[8:6];
endmodule
