// Digital circuit InOut.dig as structural Verilog
module InOut (
  input  [15:0] INR_dataIN,
  input  INR_CLK,
  input  [15:0] OUTR_dataIN,
  input  OUTR_CLK,
  input  Is_input_CLK,
  input  Valid_input,
  input  other_input,
  output [15:0] INR_dataOUT,
  output [15:0] OUTR_dataOUT,
  output Is_Input
);

  wire [15:0] register_1_q;

  Register #(.Bits(16)) register_1 (.D(INR_dataIN), .C(INR_CLK), .en(1'b1), .Q(register_1_q));
  Register #(.Bits(16)) register_2 (.D(OUTR_dataIN), .C(OUTR_CLK), .en(1'b1), .Q(OUTR_dataOUT));
  Multiplexer #(.Bits(16)) multiplexer_1 (.sel(other_input), .in_0(INR_dataIN), .in_1(register_1_q), .out(INR_dataOUT));
  D_FF d_ff_1 (.D(Valid_input), .C(Is_input_CLK), .Q(Is_Input));  // open: nQ
endmodule
