// Digital circuit Main.dig as structural Verilog
module Main (
  input  IO,
  input  CLK,
  output [15:0] DATA_out
);

  wire alu_1_c_out, alu_1_zero_output, and_1_out, and_2_out, and_3_out, and_4_out, and_5_out, and_6_out,
       Carry_Flag_q, decoder_1_add, decoder_1_add_alu, decoder_1_add_sub, decoder_1_and, decoder_1_clr,
       decoder_1_clrflags, decoder_1_comp, decoder_1_dec, decoder_1_halt, decoder_1_inc, decoder_1_isequal,
       decoder_1_jc, decoder_1_jump, decoder_1_jz, decoder_1_load, decoder_1_or, decoder_1_sl, decoder_1_slt,
       decoder_1_sr, decoder_1_store, decoder_1_sub, multiplexer_2_out, multiplexer_3_out, or_1_out,
       signal_control_1__2nd_mux, signal_control_1_alu_clk, signal_control_1_demux,
       signal_control_1_flag_clk, signal_control_1_inst_clk, signal_control_1_ist_mux,
       signal_control_1_loadsignal, signal_control_1_pc_clk, signal_control_1_ram_clk,
       signal_control_1_reg_clk, timing_and_control_1_t0, timing_and_control_1_t1, timing_and_control_1_t2,
       timing_and_control_1_t3, timing_and_control_1_t4, Zero_Flag_q;
  wire [2:0] decoder_1_rd, decoder_1_rs1, decoder_1_rs2;
  wire [3:0] priorityencoder_1_num;
  wire [10:0] multiplexer_1_out;
  wire [11:0] decoder_1_address_out, programcounter_1_ins_add;
  wire [11:11] multiplexer_1_out_2;
  wire [15:0] alu_1_alu_out, demultiplexer_1_out_0, demultiplexer_1_out_1, multiplexer_4_out,
       registerfilenew_1_do_1, registerfilenew_1_do_2;

  and and_1 (and_1_out, IO, decoder_1_halt);
  and and_2 (and_2_out, decoder_1_jz, Zero_Flag_q);
  and and_3 (and_3_out, decoder_1_jc, Carry_Flag_q);
  or or_1 (or_1_out, and_2_out, and_3_out, decoder_1_jump);
  Timing_and_Control timing_and_control_1 (
    .Timing_en(and_1_out), .CLK(CLK), .T0(timing_and_control_1_t0), .T1(timing_and_control_1_t1),
    .T2(timing_and_control_1_t2), .T3(timing_and_control_1_t3), .T4(timing_and_control_1_t4));  // open: T5, T6, T7
  Signal_Control signal_control_1 (
    .T0_in(timing_and_control_1_t0), .T1_in(timing_and_control_1_t1), .T2_in(timing_and_control_1_t2),
    .T3_in(timing_and_control_1_t3), .T4_in(timing_and_control_1_t4), .ALU(decoder_1_add_alu),
    .Ld(decoder_1_load), .St(decoder_1_store), .Ist_mux(signal_control_1_ist_mux),
    ._2nd_mux(signal_control_1__2nd_mux), .Demux(signal_control_1_demux),
    .LoadSignal(signal_control_1_loadsignal), .Inst_CLK(signal_control_1_inst_clk),
    .Ram_CLK(signal_control_1_ram_clk), .Reg_CLK(signal_control_1_reg_clk),
    .ALU_CLK(signal_control_1_alu_clk), .PC_CLK(signal_control_1_pc_clk), .Flag_CLK(signal_control_1_flag_clk));  // open: INR, OUTR, Valid_input, INR_CLK, OUTR_CLK, IS_Input_CLK, keyboard_CLK, Dis_CLK, Mux3
  ProgramCounter programcounter_1 (
    .PC_enable(1'b1), .Branch_add(decoder_1_address_out), .Simple_Branch(or_1_out),
    .CLK(signal_control_1_pc_clk), .INS_add(programcounter_1_ins_add));
  Demultiplexer #(.Bits(16)) demultiplexer_1 (
    .sel(signal_control_1_demux), .in(multiplexer_4_out), .out_0(demultiplexer_1_out_0),
    .out_1(demultiplexer_1_out_1));
  Decoder decoder_1 (
    .Instruction_in(demultiplexer_1_out_1), .CLK(signal_control_1_inst_clk), .Instruction_enable(1'b1),
    .Load(decoder_1_load), .Store(decoder_1_store), .Jump(decoder_1_jump), .JZ(decoder_1_jz),
    .JC(decoder_1_jc), .Halt(decoder_1_halt), .ADD(decoder_1_add), .SUB(decoder_1_sub),
    .IsEqual(decoder_1_isequal), .And(decoder_1_and), .Or(decoder_1_or), .Comp(decoder_1_comp),
    .SL(decoder_1_sl), .SR(decoder_1_sr), .Inc(decoder_1_inc), .Dec(decoder_1_dec), .Clr(decoder_1_clr),
    .ClrFlags(decoder_1_clrflags), .SLT(decoder_1_slt), .RD(decoder_1_rd), .RS1(decoder_1_rs1),
    .RS2(decoder_1_rs2), .Address_out(decoder_1_address_out), .ADD_ALU(decoder_1_add_alu),
    .ADD_SUB(decoder_1_add_sub));  // open: JE, JD, INR, OUTR
  RegisterFileNew registerfilenew_1 (
    .Data_in(demultiplexer_1_out_0), .Rd(decoder_1_rd), .Rs1(decoder_1_rs1), .Rs2(decoder_1_rs2),
    .CLK(signal_control_1_reg_clk), .DO_1(registerfilenew_1_do_1), .DO_2(registerfilenew_1_do_2));  // open: R1_out
  PriorityEncoder #(.Selector_Bits(4)) priorityencoder_1 (
    .in0(decoder_1_add), .in1(decoder_1_sub), .in2(decoder_1_isequal), .in3(decoder_1_and),
    .in4(decoder_1_or), .in5(decoder_1_comp), .in6(decoder_1_sl), .in7(decoder_1_sr), .in8(decoder_1_inc),
    .in9(decoder_1_dec), .in10(decoder_1_clr), .in11(decoder_1_slt), .in12(decoder_1_store), .in13(1'b0),
    .in14(1'b0), .in15(1'b0), .num(priorityencoder_1_num));  // open: any
  ALU alu_1 (
    .A_in(registerfilenew_1_do_1), .B_in(registerfilenew_1_do_2), .C_in(1'b0),
    .ContSel(priorityencoder_1_num), .CLK(signal_control_1_alu_clk), .ADD_SUB(decoder_1_add_sub),
    .ALU_out(alu_1_alu_out), .Zero_output(alu_1_zero_output), .C_out(alu_1_c_out));  // open: Is_equal
  Multiplexer #(.Bits(12)) multiplexer_1 (
    .sel(signal_control_1_ist_mux), .in_0(programcounter_1_ins_add), .in_1(decoder_1_address_out),
    .out({multiplexer_1_out_2[11], multiplexer_1_out}));
  Multiplexer multiplexer_2 (.sel(decoder_1_clrflags), .in_0(alu_1_zero_output), .in_1(1'b0), .out(multiplexer_2_out));
  Multiplexer multiplexer_3 (.sel(decoder_1_clrflags), .in_0(alu_1_c_out), .in_1(1'b0), .out(multiplexer_3_out));
  D_FF Zero_Flag (.D(multiplexer_2_out), .C(signal_control_1_flag_clk), .Q(Zero_Flag_q));  // open: nQ
  D_FF Carry_Flag (.D(multiplexer_3_out), .C(signal_control_1_flag_clk), .Q(Carry_Flag_q));  // open: nQ
  Multiplexer #(.Bits(16)) multiplexer_4 (
    .sel(signal_control_1__2nd_mux), .in_0(alu_1_alu_out), .in_1(DATA_out), .out(multiplexer_4_out));
  and and_4 (and_4_out, ~multiplexer_1_out_2[11], signal_control_1_loadsignal);  // And
  and and_5 (and_5_out, decoder_1_store, multiplexer_1_out_2[11]);
  and and_6 (and_6_out, signal_control_1_loadsignal, multiplexer_1_out_2[11]);
  ROM #(.AddrBits(11), .isProgramMemory("true"), .Bits(16)) rom_1 (
    .A(multiplexer_1_out), .sel(and_4_out), .D(DATA_out));
  RAMDualPort #(.AddrBits(11), .isProgramMemory("true"), .Bits(16)) ramdualport_1 (
    .A(multiplexer_1_out), .Din(alu_1_alu_out), .str(and_5_out), .C(signal_control_1_ram_clk),
    .ld(and_6_out), .D(DATA_out));

  // Notes on the sheet:
  //   CLK: Hz: 20
  //   contents of rom_1 (hex, n*v repeats v):
  //   e800,d,8082,e800,e,8145,80a9,400f,e800,8008,1801,ffff,0,ffff,ffff,e800,e000,1800,
  //   e800,8008,1801,ffff
endmodule
