// Digital circuit Main_Snake.dig as structural Verilog
module Main_Snake (
  input  IO,
  input  CLK,
  input  in_4,
  input  in_5,
  output [15:0] DATA_out
);

  wire alu_1_c_out, alu_1_is_equal, alu_1_zero_output, and_1_out, and_2_out, and_3_out, and_4_out, and_5_out,
       and_6_out, and_7_out, and_8_out, and_9_out, Carry_Flag_q, decoder_1_add, decoder_1_add_alu,
       decoder_1_add_sub, decoder_1_and, decoder_1_clr, decoder_1_clrflags, decoder_1_comp, decoder_1_dec,
       decoder_1_halt, decoder_1_inc, decoder_1_inr, decoder_1_isequal, decoder_1_jc, decoder_1_jd,
       decoder_1_je, decoder_1_jump, decoder_1_jz, decoder_1_load, decoder_1_or, decoder_1_outr,
       decoder_1_sl, decoder_1_slt, decoder_1_sr, decoder_1_store, decoder_1_sub, inout_1_is_input,
       keyboard_1_av, multiplexer_1_out, multiplexer_4_out, multiplexer_5_out, not_1_out, or_1_out,
       register_1_q, signal_control_1__2nd_mux, signal_control_1_alu_clk, signal_control_1_demux,
       signal_control_1_dis_clk, signal_control_1_flag_clk, signal_control_1_inr_clk,
       signal_control_1_inst_clk, signal_control_1_is_input_clk, signal_control_1_ist_mux,
       signal_control_1_keyboard_clk, signal_control_1_loadsignal, signal_control_1_mux3,
       signal_control_1_outr_clk, signal_control_1_pc_clk, signal_control_1_ram_clk,
       signal_control_1_reg_clk, timing_and_control_1_t0, timing_and_control_1_t1, timing_and_control_1_t2,
       timing_and_control_1_t3, timing_and_control_1_t4, Zero_Flag_q;
  wire [2:0] decoder_1_rd, decoder_1_rs1, decoder_1_rs2;
  wire [3:0] priorityencoder_1_num;
  wire [11:0] decoder_1_address_out, multiplexer_2_out, multiplexer_3_out, programcounter_1_ins_add,
       registerfilenew_1_r1_out;
  wire [15:0] alu_1_alu_out, demultiplexer_1_out_0, demultiplexer_1_out_1, inout_1_inr_dataout,
       inout_1_outr_dataout, keyboard_1_d, multiplexer_6_out, multiplexer_7_out, registerfilenew_1_do_1,
       registerfilenew_1_do_2;

  and and_1 (and_1_out, IO, decoder_1_halt);
  and and_2 (and_2_out, decoder_1_jz, Zero_Flag_q);
  and and_3 (and_3_out, decoder_1_jc, Carry_Flag_q);
  and and_4 (and_4_out, decoder_1_je, register_1_q);
  or or_1 (or_1_out, and_2_out, and_3_out, and_4_out, decoder_1_jump);
  Timing_and_Control timing_and_control_1 (
    .Timing_en(and_1_out), .CLK(CLK), .T0(timing_and_control_1_t0), .T1(timing_and_control_1_t1),
    .T2(timing_and_control_1_t2), .T3(timing_and_control_1_t3), .T4(timing_and_control_1_t4));  // open: T5, T6, T7
  Signal_Control signal_control_1 (
    .T0_in(timing_and_control_1_t0), .T1_in(timing_and_control_1_t1), .T2_in(timing_and_control_1_t2),
    .T3_in(timing_and_control_1_t3), .T4_in(timing_and_control_1_t4), .ALU(decoder_1_add_alu),
    .Ld(decoder_1_load), .St(decoder_1_store), .INR(decoder_1_inr), .OUTR(decoder_1_outr),
    .Valid_input(inout_1_is_input), .Ist_mux(signal_control_1_ist_mux), ._2nd_mux(signal_control_1__2nd_mux),
    .Demux(signal_control_1_demux), .LoadSignal(signal_control_1_loadsignal),
    .Inst_CLK(signal_control_1_inst_clk), .Ram_CLK(signal_control_1_ram_clk),
    .Reg_CLK(signal_control_1_reg_clk), .ALU_CLK(signal_control_1_alu_clk), .PC_CLK(signal_control_1_pc_clk),
    .Flag_CLK(signal_control_1_flag_clk), .INR_CLK(signal_control_1_inr_clk),
    .OUTR_CLK(signal_control_1_outr_clk), .IS_Input_CLK(signal_control_1_is_input_clk),
    .keyboard_CLK(signal_control_1_keyboard_clk), .Dis_CLK(signal_control_1_dis_clk),
    .Mux3(signal_control_1_mux3));
  ProgramCounter programcounter_1 (
    .PC_enable(1'b1), .Branch_add(decoder_1_address_out), .Simple_Branch(or_1_out),
    .CLK(signal_control_1_pc_clk), .INS_add(programcounter_1_ins_add));
  Demultiplexer #(.Bits(16)) demultiplexer_1 (
    .sel(signal_control_1_demux), .in(multiplexer_6_out), .out_0(demultiplexer_1_out_0),
    .out_1(demultiplexer_1_out_1));
  Decoder decoder_1 (
    .Instruction_in(demultiplexer_1_out_1), .CLK(signal_control_1_inst_clk), .Instruction_enable(1'b1),
    .Load(decoder_1_load), .Store(decoder_1_store), .Jump(decoder_1_jump), .JZ(decoder_1_jz),
    .JC(decoder_1_jc), .Halt(decoder_1_halt), .JE(decoder_1_je), .JD(decoder_1_jd), .ADD(decoder_1_add),
    .SUB(decoder_1_sub), .IsEqual(decoder_1_isequal), .And(decoder_1_and), .Or(decoder_1_or),
    .Comp(decoder_1_comp), .SL(decoder_1_sl), .SR(decoder_1_sr), .Inc(decoder_1_inc), .Dec(decoder_1_dec),
    .Clr(decoder_1_clr), .ClrFlags(decoder_1_clrflags), .SLT(decoder_1_slt), .RD(decoder_1_rd),
    .RS1(decoder_1_rs1), .RS2(decoder_1_rs2), .Address_out(decoder_1_address_out),
    .ADD_ALU(decoder_1_add_alu), .ADD_SUB(decoder_1_add_sub), .INR(decoder_1_inr), .OUTR(decoder_1_outr));
  RegisterFileNew registerfilenew_1 (
    .Data_in(demultiplexer_1_out_0), .Rd(decoder_1_rd), .Rs1(decoder_1_rs1), .Rs2(decoder_1_rs2),
    .CLK(signal_control_1_reg_clk), .DO_1(registerfilenew_1_do_1), .DO_2(registerfilenew_1_do_2),
    .R1_out(registerfilenew_1_r1_out));
  PriorityEncoder #(.Selector_Bits(4)) priorityencoder_1 (
    .in0(decoder_1_add), .in1(decoder_1_sub), .in2(decoder_1_isequal), .in3(decoder_1_and),
    .in4(decoder_1_or), .in5(decoder_1_comp), .in6(decoder_1_sl), .in7(decoder_1_sr), .in8(decoder_1_inc),
    .in9(decoder_1_dec), .in10(decoder_1_clr), .in11(decoder_1_slt), .in12(decoder_1_store),
    .in13(decoder_1_outr), .in14(1'b0), .in15(1'b0), .num(priorityencoder_1_num));  // open: any
  Keyboard keyboard_1 (.C(signal_control_1_keyboard_clk), .en(in_5), .D(keyboard_1_d), .av(keyboard_1_av));
  ALU alu_1 (
    .A_in(registerfilenew_1_do_1), .B_in(registerfilenew_1_do_2), .C_in(1'b0),
    .ContSel(priorityencoder_1_num), .CLK(signal_control_1_alu_clk), .ADD_SUB(decoder_1_add_sub),
    .ALU_out(alu_1_alu_out), .Zero_output(alu_1_zero_output), .C_out(alu_1_c_out), .Is_equal(alu_1_is_equal));
  Multiplexer multiplexer_1 (.sel(decoder_1_clrflags), .in_0(alu_1_is_equal), .in_1(1'b0), .out(multiplexer_1_out));
  Register register_1 (.D(multiplexer_1_out), .C(signal_control_1_flag_clk), .en(decoder_1_isequal), .Q(register_1_q));
  Multiplexer #(.Bits(12)) multiplexer_2 (
    .sel(decoder_1_jd), .in_0(decoder_1_address_out), .in_1(registerfilenew_1_r1_out), .out(multiplexer_2_out));
  Multiplexer #(.Bits(12)) multiplexer_3 (
    .sel(signal_control_1_ist_mux), .in_0(programcounter_1_ins_add), .in_1(multiplexer_2_out),
    .out(multiplexer_3_out));
  Multiplexer multiplexer_4 (.sel(decoder_1_clrflags), .in_0(alu_1_zero_output), .in_1(1'b0), .out(multiplexer_4_out));
  Multiplexer multiplexer_5 (.sel(decoder_1_clrflags), .in_0(alu_1_c_out), .in_1(1'b0), .out(multiplexer_5_out));
  D_FF Zero_Flag (.D(multiplexer_4_out), .C(signal_control_1_flag_clk), .Q(Zero_Flag_q));  // open: nQ
  D_FF Carry_Flag (.D(multiplexer_5_out), .C(signal_control_1_flag_clk), .Q(Carry_Flag_q));  // open: nQ
  Multiplexer #(.Bits(16)) multiplexer_6 (
    .sel(signal_control_1__2nd_mux), .in_0(alu_1_alu_out), .in_1(multiplexer_7_out), .out(multiplexer_6_out));
  not not_1 (not_1_out, multiplexer_3_out[11]);
  InOut inout_1 (
    .INR_dataIN(keyboard_1_d), .INR_CLK(signal_control_1_inr_clk), .OUTR_dataIN(alu_1_alu_out),
    .OUTR_CLK(signal_control_1_outr_clk), .Is_input_CLK(signal_control_1_is_input_clk),
    .Valid_input(keyboard_1_av), .other_input(in_4), .INR_dataOUT(inout_1_inr_dataout),
    .OUTR_dataOUT(inout_1_outr_dataout), .Is_Input(inout_1_is_input));
  and and_5 (and_5_out, ~not_1_out, decoder_1_store);  // And
  and and_6 (and_6_out, ~not_1_out, signal_control_1_loadsignal);  // And
  and and_7 (and_7_out, ~multiplexer_3_out[10], not_1_out, signal_control_1_loadsignal);  // And
  and and_8 (and_8_out, decoder_1_store, not_1_out, multiplexer_3_out[10]);
  and and_9 (and_9_out, signal_control_1_loadsignal, not_1_out, multiplexer_3_out[10]);
  Terminal terminal_1 (.D(inout_1_outr_dataout), .C(signal_control_1_dis_clk), .en(in_5));
  GraphicCard #(.graphicHeight(30), .Bits(16), .graphicWidth(30)) graphiccard_1 (
    .A(multiplexer_3_out[10:0]), .str(and_5_out), .C(signal_control_1_ram_clk), .ld(and_6_out), .B(1'b0),
    .D(alu_1_alu_out));
  ROM #(.AddrBits(10), .isProgramMemory("true"), .Bits(16)) rom_1 (
    .A(multiplexer_3_out[9:0]), .sel(and_7_out), .D(DATA_out));
  RAMDualPort #(.AddrBits(10), .isProgramMemory("true"), .Bits(16)) ramdualport_1 (
    .A(multiplexer_3_out[9:0]), .Din(alu_1_alu_out), .str(and_8_out), .C(signal_control_1_ram_clk),
    .ld(and_9_out), .D(DATA_out));
  Multiplexer #(.Bits(16)) multiplexer_7 (
    .sel(signal_control_1_mux3), .in_0(DATA_out), .in_1(inout_1_inr_dataout), .out(multiplexer_7_out));

  // Notes on the sheet:
  //   CLK: Hz: 50
  //   contents of rom_1 (hex, n*v repeats v):
  //   d,8041,e,6000,ffff,0,0,0,0,0,0,0,0,801,f000
endmodule
