// Digital circuit Memory.dig as structural Verilog
module Memory (
  input  [11:0] ADDRESS_in,
  input  Load,
  input  Store,
  input  [15:0] DATA_in,
  input  CLK,
  output [15:0] DATA_out
);

  wire and_1_out, and_2_out, and_3_out;

  and and_1 (and_1_out, ~ADDRESS_in[11], Load);  // And
  and and_2 (and_2_out, Store, ADDRESS_in[11]);
  and and_3 (and_3_out, Load, ADDRESS_in[11]);
  ROM #(.AddrBits(11), .isProgramMemory("true"), .Bits(16)) rom_1 (.A(ADDRESS_in[10:0]), .sel(and_1_out), .D(DATA_out));
  RAMDualPort #(.AddrBits(11), .Bits(16)) ramdualport_1 (
    .A(ADDRESS_in[10:0]), .Din(DATA_in), .str(and_2_out), .C(CLK), .ld(and_3_out), .D(DATA_out));

  // Notes on the sheet:
  //   contents of rom_1 (hex, n*v repeats v):
  //   e000,d,8082,e000,e,8145,8055,e000,8008,1801,0,0,0,3,2
endmodule
