// Digital circuit ProgramCounter.dig as structural Verilog
module ProgramCounter (
  input  PC_enable,
  input  [11:0] Branch_add,
  input  Simple_Branch,
  input  CLK,
  output [11:0] INS_add
);

  wire [11:0] add_1_s, multiplexer_1_out;

  Register #(.Bits(12), .isProgramCounter("true")) ProgramCounter (
    .D(multiplexer_1_out), .C(CLK), .en(PC_enable), .Q(INS_add));
  Add #(.Bits(12)) add_1 (.a(INS_add), .b(12'h1), .c_i(1'b0), .s(add_1_s));  // open: c_o
  Multiplexer #(.Bits(12)) multiplexer_1 (
    .sel(Simple_Branch), .in_0(add_1_s), .in_1(Branch_add), .out(multiplexer_1_out));
endmodule
