// Digital circuit RegisterFileNew.dig as structural Verilog
module RegisterFileNew (
  input  [15:0] Data_in,
  input  [2:0] Rd,
  input  [2:0] Rs1,
  input  [2:0] Rs2,
  input  CLK,
  output [15:0] DO_1,
  output [15:0] DO_2,
  output [11:0] R1_out
);

  wire decoder_1_out_0, decoder_1_out_1, decoder_1_out_2, decoder_1_out_3, decoder_1_out_4, decoder_1_out_5,
       decoder_1_out_6, decoder_1_out_7;
  wire [15:0] R0_q, R2_q, R3_q, R4_q, R5_q, R6_q, R7_q;
  wire [15:12] R1_q;

  Decoder #(.Selector_Bits(3)) decoder_1 (
    .sel(Rd), .out_0(decoder_1_out_0), .out_1(decoder_1_out_1), .out_2(decoder_1_out_2),
    .out_3(decoder_1_out_3), .out_4(decoder_1_out_4), .out_5(decoder_1_out_5), .out_6(decoder_1_out_6),
    .out_7(decoder_1_out_7));
  Register #(.Bits(16)) R0 (.D(Data_in), .C(CLK), .en(decoder_1_out_0), .Q(R0_q));
  Register #(.Bits(16)) R1 (.D(Data_in), .C(CLK), .en(decoder_1_out_1), .Q({R1_q, R1_out}));
  Register #(.Bits(16)) R2 (.D(Data_in), .C(CLK), .en(decoder_1_out_2), .Q(R2_q));
  Register #(.Bits(16)) R3 (.D(Data_in), .C(CLK), .en(decoder_1_out_3), .Q(R3_q));
  Register #(.Bits(16)) R4 (.D(Data_in), .C(CLK), .en(decoder_1_out_4), .Q(R4_q));
  Register #(.Bits(16)) R5 (.D(Data_in), .C(CLK), .en(decoder_1_out_5), .Q(R5_q));
  Register #(.Bits(16)) R6 (.D(Data_in), .C(CLK), .en(decoder_1_out_6), .Q(R6_q));
  Register #(.Bits(16)) R7 (.D(Data_in), .C(CLK), .en(decoder_1_out_7), .Q(R7_q));
  Multiplexer #(.Selector_Bits(3), .Bits(16)) multiplexer_1 (
    .sel(Rs1), .in_0(R0_q), .in_1({R1_q, R1_out}), .in_2(R2_q), .in_3(R3_q), .in_4(R4_q), .in_5(R5_q),
    .in_6(R6_q), .in_7(R7_q), .out(DO_1));
  Multiplexer #(.Selector_Bits(3), .Bits(16)) multiplexer_2 (
    .sel(Rs2), .in_0(R0_q), .in_1({R1_q, R1_out}), .in_2(R2_q), .in_3(R3_q), .in_4(R4_q), .in_5(R5_q),
    .in_6(R6_q), .in_7(R7_q), .out(DO_2));
endmodule
