// Digital circuit Signal Control.dig as structural Verilog
module Signal_Control (
  input  T0_in,
  input  T1_in,
  input  T2_in,
  input  T3_in,
  input  T4_in,
  input  ALU,
  input  Ld,
  input  St,
  input  INR,
  input  OUTR,
  input  Valid_input,
  output Ist_mux,
  output _2nd_mux,
  output Demux,
  output LoadSignal,
  output Inst_CLK,
  output Ram_CLK,
  output Reg_CLK,
  output ALU_CLK,
  output PC_CLK,
  output Flag_CLK,
  output INR_CLK,
  output OUTR_CLK,
  output IS_Input_CLK,
  output keyboard_CLK,
  output Dis_CLK,
  output Mux3
);

  wire and_3_out, and_4_out, and_5_out, and_6_out, and_7_out, and_8_out, and_13_out, or_1_out, or_2_out,
       or_3_out, or_4_out, or_5_out, or_7_out, or_9_out, or_10_out, or_11_out;

  or or_1 (or_1_out, Ld, INR, St);
  and and_1 (INR_CLK, T2_in, INR, Valid_input);
  and and_2 (Flag_CLK, ALU, T3_in);
  and and_3 (and_3_out, T2_in, ALU);
  and and_4 (and_4_out, T3_in, ALU);
  and and_5 (and_5_out, T3_in, or_2_out);
  and and_6 (and_6_out, T2_in, or_1_out);
  or or_2 (or_2_out, Ld, INR);
  and and_7 (and_7_out, T2_in, Ld);
  and and_8 (and_8_out, T3_in, St);
  or or_3 (or_3_out, Ld, INR, ALU);
  or or_4 (or_4_out, ALU, OUTR, St);
  or or_5 (or_5_out, and_3_out, and_4_out);
  or or_6 (Ram_CLK, and_7_out, and_8_out);
  and and_9 (Reg_CLK, or_3_out, T3_in);
  and and_10 (ALU_CLK, or_4_out, T2_in);
  and and_11 (OUTR_CLK, OUTR, T3_in);
  and and_12 (Dis_CLK, OUTR, T4_in);
  and and_13 (and_13_out, or_11_out, Ld);
  or or_7 (or_7_out, T0_in, T1_in, and_5_out, and_6_out);
  or or_8 (LoadSignal, or_10_out, and_13_out);
  or or_9 (or_9_out, T2_in, T3_in, T4_in);
  and and_14 (Mux3, INR, or_9_out);
  or or_10 (or_10_out, T0_in, T1_in);
  or or_11 (or_11_out, T2_in, T3_in);
  PriorityEncoder priorityencoder_1 (.in0(or_10_out), .in1(or_11_out), .num(Ist_mux));  // open: any
  PriorityEncoder priorityencoder_2 (.in0(or_5_out), .in1(or_7_out), .num(_2nd_mux));  // open: any
  PriorityEncoder priorityencoder_3 (.in0(or_9_out), .in1(or_10_out), .num(Demux));  // open: any

  assign Inst_CLK = T1_in;
  assign IS_Input_CLK = T1_in;
  assign keyboard_CLK = INR_CLK;
  assign PC_CLK = T4_in;
endmodule
