// Digital circuit Test Verilog.dig as structural Verilog
module Test_Verilog (
  input  IO,
  input  CLK,
  input  C_Flag,
  input  [15:0] RAM_Data_out,
  output Ram_Clk,
  output [15:0] RAM_Data_in,
  output [11:0] RAM_Address_in,
  output Store,
  output Load
);

  wire decoder_1_add, decoder_1_add_alu, decoder_1_and, decoder_1_clr, decoder_1_comp, decoder_1_dec,
       decoder_1_inc, decoder_1_isequal, decoder_1_jump, decoder_1_load, decoder_1_or, decoder_1_sl,
       decoder_1_slt, decoder_1_sr, decoder_1_sub, signal_control_1__2nd_mux, signal_control_1_alu_clk,
       signal_control_1_demux, signal_control_1_inst_clk, signal_control_1_ist_mux, signal_control_1_pc_clk,
       signal_control_1_reg_clk, timing_and_control_1_t0, timing_and_control_1_t1, timing_and_control_1_t2,
       timing_and_control_1_t3, timing_and_control_1_t4;
  wire [2:0] decoder_1_rd, decoder_1_rs1, decoder_1_rs2;
  wire [3:0] priorityencoder_1_num;
  wire [11:0] decoder_1_address_out, programcounter_1_ins_add;
  wire [15:0] demultiplexer_1_out_0, demultiplexer_1_out_1, multiplexer_2_out, registerfilenew_1_do_1,
       registerfilenew_1_do_2;

  Timing_and_Control timing_and_control_1 (
    .Timing_en(IO), .CLK(CLK), .T0(timing_and_control_1_t0), .T1(timing_and_control_1_t1),
    .T2(timing_and_control_1_t2), .T3(timing_and_control_1_t3), .T4(timing_and_control_1_t4));  // open: T5, T6, T7
  Signal_Control signal_control_1 (
    .T0_in(timing_and_control_1_t0), .T1_in(timing_and_control_1_t1), .T2_in(timing_and_control_1_t2),
    .T3_in(timing_and_control_1_t3), .T4_in(timing_and_control_1_t4), .ALU(decoder_1_add_alu),
    .Ld(decoder_1_load), .St(Store), .INR(Store), .Ist_mux(signal_control_1_ist_mux),
    ._2nd_mux(signal_control_1__2nd_mux), .Demux(signal_control_1_demux), .LoadSignal(Load),
    .Inst_CLK(signal_control_1_inst_clk), .Ram_CLK(Ram_Clk), .Reg_CLK(signal_control_1_reg_clk),
    .ALU_CLK(signal_control_1_alu_clk), .PC_CLK(signal_control_1_pc_clk));  // open: OUTR, Valid_input, Flag_CLK, INR_CLK, OUTR_CLK, IS_Input_CLK, keyboard_CLK, Dis_CLK, Mux3
  ProgramCounter programcounter_1 (
    .PC_enable(1'b1), .Branch_add(decoder_1_address_out), .Simple_Branch(decoder_1_jump),
    .CLK(signal_control_1_pc_clk), .INS_add(programcounter_1_ins_add));
  Demultiplexer #(.Bits(16)) demultiplexer_1 (
    .sel(signal_control_1_demux), .in(multiplexer_2_out), .out_0(demultiplexer_1_out_0),
    .out_1(demultiplexer_1_out_1));
  Decoder decoder_1 (
    .Instruction_in(demultiplexer_1_out_1), .CLK(signal_control_1_inst_clk), .Instruction_enable(1'b1),
    .Load(decoder_1_load), .Store(Store), .Jump(decoder_1_jump), .ADD(decoder_1_add), .SUB(decoder_1_sub),
    .IsEqual(decoder_1_isequal), .And(decoder_1_and), .Or(decoder_1_or), .Comp(decoder_1_comp),
    .SL(decoder_1_sl), .SR(decoder_1_sr), .Inc(decoder_1_inc), .Dec(decoder_1_dec), .Clr(decoder_1_clr),
    .SLT(decoder_1_slt), .RD(decoder_1_rd), .RS1(decoder_1_rs1), .RS2(decoder_1_rs2),
    .Address_out(decoder_1_address_out), .ADD_ALU(decoder_1_add_alu));  // open: JZ, JC, Halt, JE, JD, ClrFlags, ADD_SUB, INR, OUTR
  RegisterFileNew registerfilenew_1 (
    .Data_in(demultiplexer_1_out_0), .Rd(decoder_1_rd), .Rs1(decoder_1_rs1), .Rs2(decoder_1_rs2),
    .CLK(signal_control_1_reg_clk), .DO_1(registerfilenew_1_do_1), .DO_2(registerfilenew_1_do_2));  // open: R1_out
  PriorityEncoder #(.Selector_Bits(4)) priorityencoder_1 (
    .in0(decoder_1_add), .in1(decoder_1_sub), .in2(decoder_1_isequal), .in3(decoder_1_and),
    .in4(decoder_1_or), .in5(decoder_1_comp), .in6(decoder_1_sl), .in7(decoder_1_sr), .in8(decoder_1_inc),
    .in9(decoder_1_dec), .in10(decoder_1_clr), .in11(decoder_1_slt), .in12(Store), .in13(1'b0), .in14(1'b0),
    .in15(1'b0), .num(priorityencoder_1_num));  // open: any
  // ALU alu_1: pin names not known; wires that end beside it: registerfilenew_1_do_1, registerfilenew_1_do_2, C_Flag, priorityencoder_1_num, signal_control_1_alu_clk, RAM_Data_in
  Multiplexer #(.Bits(12)) multiplexer_1 (
    .sel(signal_control_1_ist_mux), .in_0(programcounter_1_ins_add), .in_1(decoder_1_address_out),
    .out(RAM_Address_in));
  Multiplexer #(.Bits(16)) multiplexer_2 (
    .sel(signal_control_1__2nd_mux), .in_0(RAM_Data_in), .in_1(RAM_Data_out), .out(multiplexer_2_out));

  // Notes on the sheet:
  //   CLK: Hz: 20
endmodule
