// Digital circuit Timing and Control.dig as structural Verilog
module Timing_and_Control (
  input  Timing_en,
  input  CLK,
  output T0,
  output T1,
  output T2,
  output T3,
  output T4,
  output T5,
  output T6,
  output T7
);

  wire [2:0] counter_1_out;

  Counter #(.Bits(3)) counter_1 (.en(Timing_en), .C(CLK), .clr(T4), .out(counter_1_out));  // open: ovf
  Decoder #(.Selector_Bits(3)) decoder_1 (
    .sel(counter_1_out), .out_0(T0), .out_1(T1), .out_2(T2), .out_3(T3), .out_4(T4), .out_5(T5), .out_6(T6),
    .out_7(T7));

  // Notes on the sheet:
  //   CLK: Hz: 2
endmodule
